// Logisim project more_advance_p2.circ as structural Verilog: 5 circuits, main circuit four_bit_computer
// reset
module four_bit_computer (
);

  wire A_writing, and_1_out, and_2_out, and_3_out, clock, d_ff_1_q, demultiplexer_1_out6,
       demultiplexer_1_out7, LE, nor_1_out, nor_2_out, or_1_out, or_2_out, PC_carry, reset,
       three_bit_or_with_fourth_bit_and_out_3, toggled_register_1_writing, toggled_register_2_writing;
  wire [0:0] demultiplexer_1_out0;
  wire [1:0] demultiplexer_1_out2;
  wire [2:0] bcd_to_7_segment_decoder_1_p1, bcd_to_7_segment_decoder_2_p1, bcd_to_7_segment_decoder_3_p1,
       MainRom_data;
  wire [3:3] MainRom_data_2;
  wire [6:0] PC_q;

  Counter #(.max('h7f), .trigger("falling"), .width(7)) PC (
    .clr(reset), .load(LE), .up(1'b1), .count(1'b1), .clk(clock), .D({4'b0000, MainRom_data}),
    .carry(PC_carry), .Q(PC_q));
  ROM #(.addrWidth(7), .dataWidth(4)) MainRom (.addr(PC_q), .data({MainRom_data_2[3], MainRom_data}));
  Clock #(.phaseOffset(1)) GlobalClock (.out(clock));
  Button GlobalReset (.out(reset));
  _7_Segment_Display u_7_segment_display_1 ();  // open: g, f, a, b, e, d, c, dp
  // BCD_to_7_Segment_decoder bcd_to_7_segment_decoder_1: pin names not known; wires that end beside it: {1'b0, bcd_to_7_segment_decoder_1_p1}
  _7_Segment_Display u_7_segment_display_2 ();  // open: g, f, a, b, e, d, c, dp
  // BCD_to_7_Segment_decoder bcd_to_7_segment_decoder_2: pin names not known; wires that end beside it: {1'b0, bcd_to_7_segment_decoder_2_p1}
  _7_Segment_Display u_7_segment_display_3 ();  // open: g, f, a, b, e, d, c, dp
  // BCD_to_7_Segment_decoder bcd_to_7_segment_decoder_3: pin names not known; wires that end beside it: {1'b0, bcd_to_7_segment_decoder_3_p1}
  Demultiplexer #(.select(3)) demultiplexer_1 (
    .out0(demultiplexer_1_out0[0]), .out1(demultiplexer_1_out2[0]), .out2(demultiplexer_1_out2[1]),
    .out6(demultiplexer_1_out6), .out7(demultiplexer_1_out7), .in(MainRom_data_2[3]), .sel(MainRom_data));  // open: out3, out4, out5
  and and_1 (and_1_out, demultiplexer_1_out0[0], nor_1_out);
  and_3_1 three_bit_or_with_fourth_bit_and (
    .three_bit_bus(bcd_to_7_segment_decoder_3_p1), .one_bit(demultiplexer_1_out6),
    .out_3(three_bit_or_with_fourth_bit_and_out_3));
  or or_1 (or_1_out, demultiplexer_1_out7, three_bit_or_with_fourth_bit_and_out_3);
  D_Flip_Flop d_ff_1 (.D(or_1_out), .clk(clock), .Q(d_ff_1_q), .preset(or_1_out), .reset(or_2_out));  // open: Qn
  or or_2 (or_2_out, MainRom_data_2[3], reset);
  toggled_register A (
    .DataIn(MainRom_data), .RegX(bcd_to_7_segment_decoder_2_p1), .RegY(bcd_to_7_segment_decoder_3_p1),
    .select_in(demultiplexer_1_out2), .toggle(and_1_out), .is_write(nor_2_out), .clock(clock), .Reset(reset),
    .writing(A_writing), .DataOut(bcd_to_7_segment_decoder_1_p1));
  and and_2 (and_2_out, demultiplexer_1_out2[0], nor_1_out);
  D_Flip_Flop d_ff_2 (.D(d_ff_1_q), .clk(clock), .Q(LE), .preset(d_ff_1_q));  // open: Qn, reset
  LedBar #(.matrixcols(9)) MainOutput (
    .led0(bcd_to_7_segment_decoder_1_p1[2]), .led1(bcd_to_7_segment_decoder_1_p1[1]),
    .led2(bcd_to_7_segment_decoder_1_p1[0]), .led3(bcd_to_7_segment_decoder_2_p1[2]),
    .led4(bcd_to_7_segment_decoder_2_p1[1]), .led5(bcd_to_7_segment_decoder_2_p1[0]),
    .led6(bcd_to_7_segment_decoder_3_p1[2]), .led7(bcd_to_7_segment_decoder_3_p1[1]),
    .led8(bcd_to_7_segment_decoder_3_p1[0]));
  nor nor_1 (nor_1_out, A_writing, toggled_register_1_writing, toggled_register_2_writing);
  nor nor_2 (nor_2_out, demultiplexer_1_out0[0], demultiplexer_1_out2[0], demultiplexer_1_out2[1]);
  and and_3 (and_3_out, demultiplexer_1_out2[1], nor_1_out);
  toggled_register toggled_register_1 (
    .DataIn(MainRom_data), .RegX(bcd_to_7_segment_decoder_1_p1), .RegY(bcd_to_7_segment_decoder_3_p1),
    .select_in({demultiplexer_1_out2[1], demultiplexer_1_out0[0]}), .toggle(and_2_out), .is_write(nor_2_out),
    .clock(clock), .Reset(reset), .writing(toggled_register_1_writing),
    .DataOut(bcd_to_7_segment_decoder_2_p1));
  toggled_register toggled_register_2 (
    .DataIn(MainRom_data), .RegX(bcd_to_7_segment_decoder_1_p1), .RegY(bcd_to_7_segment_decoder_2_p1),
    .select_in({demultiplexer_1_out2[0], demultiplexer_1_out0[0]}), .toggle(and_3_out), .is_write(nor_2_out),
    .clock(clock), .Reset(reset), .writing(toggled_register_2_writing),
    .DataOut(bcd_to_7_segment_decoder_3_p1));
  // also tied to GND on the sheet: PC_carry

  // Notes on the sheet:
  //   contents of MainRom (hex, n*v repeats v):
  //   a 0 8 7 8 3 9 4 8 1 9 6 8 0 9 7 9 3 a 4 9 1 a 6 9 0 a 7 8 4 a 3 8 6 a 1 e
endmodule

module Add_Sub (
  input  [2:0] old_value,
  input  [2:0] value,
  input  sel_add_sub,
  output [2:0] new_value
);

  wire subtractor_1_bout;
  wire [2:0] adder_1_out, subtractor_1_out;

  Adder #(.width(3)) adder_1 (.a(old_value), .b(value), .out(adder_1_out));  // open: cin, cout
  Subtractor #(.width(3)) subtractor_1 (
    .a(old_value), .b(value), .out(subtractor_1_out), .bout(subtractor_1_bout));  // open: bin
  Multiplexer #(.width(3)) multiplexer_1 (
    .in0(adder_1_out), .in1(subtractor_1_out), .out(new_value), .sel(sel_add_sub));
  // also tied to GND on the sheet: subtractor_1_bout
endmodule

module toggled_register (
  input  [2:0] DataIn,
  input  [2:0] RegX,
  input  [2:0] RegY,
  input  [1:0] select_in,
  input  toggle,
  input  is_write,
  input  clock,
  input  Reset,
  output writing,
  output [2:0] DataOut
);

  wire d_ff_1_q;
  wire [2:0] multiplexer_1_out;

  D_Flip_Flop d_ff_1 (.D(toggle), .clk(clock), .Q(d_ff_1_q), .preset(toggle), .reset(Reset));  // open: Qn
  Multiplexer #(.select(2), .width(3)) multiplexer_1 (
    .in0(DataIn), .in1(RegX), .in2(RegY), .out(multiplexer_1_out), .sel(select_in));  // open: in3
  and and_1 (writing, d_ff_1_q, is_write);
  Register #(.width(3)) register_1 (.D(multiplexer_1_out), .en(writing), .clk(clock), .Q(DataOut), .clr(Reset));
endmodule

module and_3_1 (
  input  [2:0] three_bit_bus,
  input  one_bit,
  output out_3
);

  wire or_1_out;

  or or_1 (or_1_out, three_bit_bus[0], three_bit_bus[1], three_bit_bus[2]);
  and and_1 (out_3, or_1_out, one_bit);
endmodule

module advance_splitter (
  input  [1:0] two,
  input  [2:0] three,
  input  [3:0] four,
  input  [4:0] five,
  input  [5:0] six,
  input  [6:0] seven,
  input  [7:0] eight,
  output [1:0] Otwo,
  output [2:0] Othree,
  output [3:0] Ofour,
  output [4:0] oFive,
  output [5:0] oSix,
  output [6:0] oSeven,
  output [7:0] oEight
);


  assign five = eight[4:0];
  assign four = eight[3:0];
  assign oEight = eight;
  assign oFive = eight[4:0];
  assign Ofour = eight[3:0];
  assign oSeven = eight[6:0];
  assign oSix = eight[5:0];
  assign Othree = eight[2:0];
  assign Otwo = eight[1:0];
  assign seven = eight[6:0];
  assign six = eight[5:0];
  assign three = eight[2:0];
  assign two = eight[1:0];
endmodule
