// Logisim project three_bit_comp.circ as structural Verilog: 1 circuit, main circuit four_bit_computer
// reset
module four_bit_computer (
);

  wire d_ff_1_q, d_ff_2_q, d_ff_3_q, d_ff_4_q, d_ff_5_q, demultiplexer_1_out0, demultiplexer_1_out1,
       demultiplexer_1_out2, demultiplexer_1_out3, demultiplexer_1_out4, demultiplexer_1_out5,
       demultiplexer_1_out6, demultiplexer_1_out7, GlobalClock_out, GlobalReset_out, or_1_out, or_2_out,
       or_3_out, or_4_out, or_5_out, PC_carry;
  wire [2:0] bcd_to_7_segment_decoder_1_p1, bcd_to_7_segment_decoder_2_p1, bcd_to_7_segment_decoder_3_p1,
       MainRom_data_2, undriven;
  wire [3:3] MainRom_data;
  wire [6:0] PC_q;

  Counter #(.max('h7f), .trigger("falling"), .width(7)) PC (
    .clr(or_1_out), .load(d_ff_4_q), .up(1'b1), .count(1'b1), .clk(GlobalClock_out),
    .D({4'b0000, MainRom_data_2}), .carry(PC_carry), .Q(PC_q));
  or or_1 (or_1_out, GlobalReset_out, GlobalReset_out);
  ROM #(.addrWidth(7), .dataWidth(4)) MainRom (.addr(PC_q), .data({MainRom_data[3], MainRom_data_2}));
  Clock GlobalClock (.out(GlobalClock_out));
  Button GlobalReset (.out(GlobalReset_out));
  _7_Segment_Display u_7_segment_display_1 ();  // open: g, f, a, b, e, d, c, dp
  // BCD_to_7_Segment_decoder bcd_to_7_segment_decoder_1: pin names not known; wires that end beside it: {1'b0, bcd_to_7_segment_decoder_1_p1}
  _7_Segment_Display u_7_segment_display_2 ();  // open: g, f, a, b, e, d, c, dp
  // BCD_to_7_Segment_decoder bcd_to_7_segment_decoder_2: pin names not known; wires that end beside it: {1'b0, bcd_to_7_segment_decoder_2_p1}
  _7_Segment_Display u_7_segment_display_3 ();  // open: g, f, a, b, e, d, c, dp
  // BCD_to_7_Segment_decoder bcd_to_7_segment_decoder_3: pin names not known; wires that end beside it: {1'b0, bcd_to_7_segment_decoder_3_p1}
  Demultiplexer #(.select(3)) demultiplexer_1 (
    .out0(demultiplexer_1_out0), .out1(demultiplexer_1_out1), .out2(demultiplexer_1_out2),
    .out3(demultiplexer_1_out3), .out4(demultiplexer_1_out4), .out5(demultiplexer_1_out5),
    .out6(demultiplexer_1_out6), .out7(demultiplexer_1_out7), .in(MainRom_data[3]), .sel(MainRom_data_2));
  // Binary_to_BCD_converter #(.binvalue(4)) binary_to_bcd_converter_1: pin names not known; wires that end beside it: {1'b0, MainRom_data_2}, GlobalClock_out
  D_Flip_Flop d_ff_1 (
    .D(or_2_out), .clk(GlobalClock_out), .Q(d_ff_1_q), .preset(or_2_out), .reset(MainRom_data[3]));  // open: Qn
  or or_2 (or_2_out, demultiplexer_1_out0, demultiplexer_1_out3, demultiplexer_1_out4, demultiplexer_1_out6);
  Register #(.width(3)) A (
    .D(undriven), .en(d_ff_1_q), .clk(GlobalClock_out), .Q(bcd_to_7_segment_decoder_1_p1),
    .clr(GlobalReset_out));
  or or_3 (or_3_out, demultiplexer_1_out1, demultiplexer_1_out3, demultiplexer_1_out5, demultiplexer_1_out6);
  D_Flip_Flop d_ff_2 (
    .D(demultiplexer_1_out7), .clk(GlobalClock_out), .Q(d_ff_2_q), .preset(demultiplexer_1_out7),
    .reset(or_4_out));  // open: Qn
  or or_4 (or_4_out, MainRom_data[3], GlobalReset_out);
  D_Flip_Flop d_ff_3 (
    .D(or_3_out), .clk(GlobalClock_out), .Q(d_ff_3_q), .preset(or_3_out), .reset(MainRom_data[3]));  // open: Qn
  D_Flip_Flop d_ff_4 (.D(d_ff_2_q), .clk(GlobalClock_out), .Q(d_ff_4_q));  // open: Qn, preset, reset
  Register #(.width(3)) B (
    .D(undriven), .en(d_ff_3_q), .clk(GlobalClock_out), .Q(bcd_to_7_segment_decoder_2_p1),
    .clr(GlobalReset_out));
  LedBar #(.matrixcols(9)) MainOutput (
    .led0(bcd_to_7_segment_decoder_1_p1[2]), .led1(bcd_to_7_segment_decoder_1_p1[1]),
    .led2(bcd_to_7_segment_decoder_1_p1[0]), .led3(bcd_to_7_segment_decoder_2_p1[2]),
    .led4(bcd_to_7_segment_decoder_2_p1[1]), .led5(bcd_to_7_segment_decoder_2_p1[0]),
    .led6(bcd_to_7_segment_decoder_3_p1[2]), .led7(bcd_to_7_segment_decoder_3_p1[1]),
    .led8(bcd_to_7_segment_decoder_3_p1[0]));
  D_Flip_Flop d_ff_5 (
    .D(or_5_out), .clk(GlobalClock_out), .Q(d_ff_5_q), .preset(or_5_out), .reset(MainRom_data[3]));  // open: Qn
  or or_5 (or_5_out, demultiplexer_1_out2, demultiplexer_1_out4, demultiplexer_1_out5, demultiplexer_1_out6);
  Register #(.width(3)) C (
    .D(undriven), .en(d_ff_5_q), .clk(GlobalClock_out), .Q(bcd_to_7_segment_decoder_3_p1),
    .clr(GlobalReset_out));
  // also tied to GND on the sheet: PC_carry

  // Notes on the sheet:
  //   contents of MainRom (hex, n*v repeats v):
  //   8 7 d 0 8 3 9 4 8 1 9 6 8 0 9 7 9 3 a 4 9 1 a 6 9 0 a 7 8 4 a 3 8 6 a 1 f 6
endmodule
